// Logisim project 01-从零开始.circ as structural Verilog: 3 circuits, main circuit main
module main (
  input  x,
  input  y,
  input  s,
  output z
);

  wire and_1_out, or_1_out;

  and and_1 (and_1_out, x, y);
  or or_1 (or_1_out, x, y);
  Multiplexer #(.enable("false")) multiplexer_1 (.in0(and_1_out), .in1(or_1_out), .out(z), .sel(s));
endmodule

module \从零开始  (
  input  x,
  input  y,
  input  s,
  output z
);

  wire and_1_out, or_1_out;

  // Probe on x
  and and_1 (and_1_out, x, y);
  or or_1 (or_1_out, x, y);
  Multiplexer multiplexer_1 (.in0(and_1_out), .in1(or_1_out), .out(z), .sel(s));  // open: en
endmodule

module \测试电路  (
);

  \从零开始  \u_从零开始_1  ();  // open: x, y, z, s
endmodule
