// Logisim project 02-自动生成电路.circ as structural Verilog: 1 circuit, main circuit main
module main (
  input  x,
  input  y,
  input  Cin,
  output Sum,
  output Cout
);

  wire and_1_out, and_2_out, and_3_out, and_4_out, and_5_out, and_6_out, and_7_out, and_8_out, and_9_out,
       and_10_out, and_11_out, not_1_out, not_2_out, not_3_out, not_4_out, not_5_out, not_6_out, or_1_out,
       or_3_out, or_4_out;

  not not_1 (not_1_out, x);
  not not_2 (not_2_out, y);
  not not_3 (not_3_out, x);
  not not_4 (not_4_out, y);
  and and_1 (and_1_out, y, Cin);
  and and_2 (and_2_out, x, Cin);
  and and_3 (and_3_out, not_1_out, not_2_out);
  and and_4 (and_4_out, not_3_out, y);
  not not_5 (not_5_out, Cin);
  and and_5 (and_5_out, x, not_4_out);
  not not_6 (not_6_out, Cin);
  and and_6 (and_6_out, x, y);
  or or_1 (or_1_out, and_1_out, and_2_out);
  and and_7 (and_7_out, x, y);
  and and_8 (and_8_out, and_3_out, Cin);
  and and_9 (and_9_out, and_4_out, not_5_out);
  and and_10 (and_10_out, and_5_out, not_6_out);
  and and_11 (and_11_out, and_6_out, Cin);
  or or_2 (Cout, or_1_out, and_7_out);
  or or_3 (or_3_out, and_8_out, and_9_out);
  or or_4 (or_4_out, and_10_out, and_11_out);
  or or_5 (Sum, or_3_out, or_4_out);
endmodule
