// Logisim project 00-测试电路.circ as structural Verilog: 1 circuit, main circuit 从零开始
module \从零开始  (
  input  [3:0] x,
  input  [3:0] y,
  input  s,
  output [3:0] z
);

  wire [3:0] and_1_out, or_1_out;

  // Probe on y
  // Probe on x
  assign and_1_out = x & y;  // AND_Gate and_1, 4 bits wide
  assign or_1_out = x | y;  // OR_Gate or_1, 4 bits wide
  Multiplexer #(.width(4), .enable("false")) multiplexer_1 (.in0(and_1_out), .in1(or_1_out), .out(z), .sel(s));
endmodule
